# Fritzing sketch message-thing-device (saved by Fritzing 0.9.3b)
breadboards: 1

parts:
  LCD1 = LCD screen
  LCM1602_IIC1 = LCM1602 IIC [part_number="LCM1602 IIC" chip_label="LCM1602 IIC" package="DIP (Dual Inline) [THT]"]
  S1 = Pushbutton [package="[THT]"]
  S2 = Pushbutton [package="[THT]"]
  S3 = Pushbutton [package="[THT]"]
  R1 = Resistor [tolerance=±5% resistance=10 package="0805 [SMD]"]
  R2 = Resistor [tolerance=±5% resistance=10 package="0805 [SMD]"]
  R3 = Resistor [tolerance=±5% resistance=10 package="0805 [SMD]"]
  LED1 = LED - 3mm [color="Red (633nm)" package="3 mm [THT]"]
  U1 = NodeMCU V3.0

nets:
  VSS: LCD1.VSS, LCM1602_IIC1.VSS
  VDD: LCD1.VDD, LCM1602_IIC1.VDD
  N1: LCD1.V0, LCM1602_IIC1.V0
  N2: LCD1.RS, LCM1602_IIC1.RS
  N3: LCD1.R/W, LCM1602_IIC1.RW
  N4: LCD1.E, LCM1602_IIC1.E
  N5: LCD1.DB0, LCM1602_IIC1.D0
  N6: LCD1.DB1, LCM1602_IIC1.D1
  N7: LCD1.DB2, LCM1602_IIC1.D2
  N8: LCD1.DB3, LCM1602_IIC1.D3
  N9: LCD1.DB4, LCM1602_IIC1.D4
  N10: LCD1.DB5, LCM1602_IIC1.D5
  N11: LCD1.DB6, LCM1602_IIC1.D6
  N12: LCD1.DB7, LCM1602_IIC1.D7
  N13: LCD1.LED+, LCM1602_IIC1.A
  N14: LCD1.LED-, LCM1602_IIC1.K
  N15: LCM1602_IIC1.GND, R1.Pin_1, R2.Pin_1, R3.Pin_1, LED1.cathode, U1.GND#6, U1.GND#13, U1.GND#16, U1.GND#33
  VCC: LCM1602_IIC1.VCC, S1.Pin_3, S1.Pin_4, S2.Pin_3, S2.Pin_4, S3.Pin_3, S3.Pin_4, U1.Vin
  N16: LCM1602_IIC1.SDA, U1.D2
  N17: LCM1602_IIC1.SCL, U1.D1
  N18: S1.Pin_1, S1.Pin_2, R3.Pin_0, U1.D7
  N19: S2.Pin_1, S2.Pin_2, R1.Pin_0, U1.D5
  N20: S3.Pin_1, S3.Pin_2, R2.Pin_0, U1.D8
  N21: LED1.anode, U1.D6

custom parts:
  LCM1602 IIC: I2C-Module to use a 1602 or 2004 LCD on with the wire.h libory Serial LCD Modul
  NodeMCU V3.0: ESP8266 based NodeMCU
